// Logisim project 1-bit Full Subtractor.circ as structural Verilog: 1 circuit, main circuit main
module main (
  input  Bin,
  input  x,
  input  y,
  output D,
  output Bout
);

  wire and_1_out, and_2_out, not_1_out, not_2_out, xor_1_out;

  not not_1 (not_1_out, x);
  xor xor_1 (xor_1_out, x, y);
  and and_1 (and_1_out, y, not_1_out);
  not not_2 (not_2_out, xor_1_out);
  xor xor_2 (D, Bin, xor_1_out);
  and and_2 (and_2_out, not_2_out, Bin);
  or or_1 (Bout, and_2_out, and_1_out);
endmodule
