// Logisim project 1-bit Half Adder.circ as structural Verilog: 1 circuit, main circuit main
module main (
  input  x,
  input  y,
  output sum,
  output cout
);

  xor xor_1 (sum, x, y);
  and and_1 (cout, x, y);
endmodule
