// Logisim project 1-bit Half Subtractor.circ as structural Verilog: 1 circuit, main circuit main
module main (
  input  x,
  input  y,
  output D,
  output Bout
);

  wire not_1_out;

  not not_1 (not_1_out, x);
  xor xor_1 (D, x, y);
  and and_1 (Bout, not_1_out, not_1_out, y);
endmodule
