// Logisim project 2-bit Full Adder.circ as structural Verilog: 1 circuit, main circuit main
module main (
  input  x2,
  input  y2,
  input  x1,
  input  y1,
  input  Cin,
  output S2,
  output Cout2,
  output S1
);

  wire and_1_out, and_2_out, and_3_out, and_4_out, or_2_out, xor_1_out, xor_2_out;

  xor xor_1 (xor_1_out, x2, y2);
  and and_1 (and_1_out, x2, y2);
  xor xor_2 (xor_2_out, x1, y1);
  and and_2 (and_2_out, x1, y1);
  xor xor_3 (S2, xor_1_out, or_2_out);
  and and_3 (and_3_out, xor_1_out, or_2_out);
  xor xor_4 (S1, xor_2_out, Cin);
  and and_4 (and_4_out, xor_2_out, Cin);
  or or_1 (Cout2, and_3_out, and_1_out);
  or or_2 (or_2_out, and_4_out, and_2_out);

  // Notes on the sheet:
  //   Cout1
endmodule
