// Logisim project 2-bit Full Subtractor.circ as structural Verilog: 1 circuit, main circuit main
module main (
  input  Bin,
  input  x1,
  input  y1,
  input  x2,
  input  y2,
  output D1,
  output D2,
  output Bout2
);

  wire and_1_out, and_2_out, and_3_out, and_4_out, not_1_out, not_2_out, not_3_out, not_4_out, or_1_out,
       xor_1_out, xor_2_out;

  not not_1 (not_1_out, x1);
  not not_2 (not_2_out, x2);
  xor xor_1 (xor_1_out, x1, y1);
  and and_1 (and_1_out, y1, not_1_out);
  xor xor_2 (xor_2_out, x2, y2);
  and and_2 (and_2_out, y2, not_2_out);
  not not_3 (not_3_out, xor_1_out);
  not not_4 (not_4_out, xor_2_out);
  xor xor_3 (D1, Bin, xor_1_out);
  and and_3 (and_3_out, not_3_out, Bin);
  xor xor_4 (D2, or_1_out, xor_2_out);
  and and_4 (and_4_out, not_4_out, or_1_out);
  or or_1 (or_1_out, and_3_out, and_1_out);
  or or_2 (Bout2, and_4_out, and_2_out);

  // Notes on the sheet:
  //   Bout1
endmodule
