// Logisim project 4-bit Full Adder.circ as structural Verilog: 1 circuit, main circuit main
module main (
  input  x4,
  input  y4,
  input  x3,
  input  y3,
  input  x2,
  input  y2,
  input  x1,
  input  y1,
  input  Cin,
  output S4,
  output Cout4,
  output S3,
  output S2,
  output S1
);

  wire and_1_out, and_2_out, and_3_out, and_4_out, and_5_out, and_6_out, and_7_out, and_8_out, or_2_out,
       or_3_out, or_4_out, xor_1_out, xor_2_out, xor_3_out, xor_4_out;

  and and_1 (and_1_out, x3, y3);
  xor xor_1 (xor_1_out, x4, y4);
  and and_2 (and_2_out, x4, y4);
  xor xor_2 (xor_2_out, x3, y3);
  xor xor_3 (xor_3_out, x2, y2);
  and and_3 (and_3_out, x2, y2);
  xor xor_4 (xor_4_out, x1, y1);
  and and_4 (and_4_out, x1, y1);
  xor xor_5 (S4, xor_1_out, or_2_out);
  and and_5 (and_5_out, xor_1_out, or_2_out);
  xor xor_6 (S3, xor_2_out, or_3_out);
  and and_6 (and_6_out, xor_2_out, or_3_out);
  xor xor_7 (S2, xor_3_out, or_4_out);
  and and_7 (and_7_out, xor_3_out, or_4_out);
  xor xor_8 (S1, xor_4_out, Cin);
  and and_8 (and_8_out, xor_4_out, Cin);
  or or_1 (Cout4, and_5_out, and_2_out);
  or or_2 (or_2_out, and_6_out, and_1_out);
  or or_3 (or_3_out, and_7_out, and_3_out);
  or or_4 (or_4_out, and_8_out, and_4_out);

  // Notes on the sheet:
  //   Cout3
  //   Cout2
  //   Cout1
endmodule
