// Logisim project 4-bit Full Subtractor.circ as structural Verilog: 1 circuit, main circuit main
module main (
  input  Bin,
  input  x1,
  input  y1,
  input  x2,
  input  y2,
  input  x3,
  input  y3,
  input  x4,
  input  y4,
  output D1,
  output D2,
  output D3,
  output D4,
  output Bout4
);

  wire and_1_out, and_2_out, and_3_out, and_4_out, and_5_out, and_6_out, and_7_out, and_8_out, not_1_out,
       not_2_out, not_3_out, not_4_out, not_5_out, not_6_out, not_7_out, not_8_out, or_1_out, or_2_out,
       or_3_out, xor_1_out, xor_2_out, xor_3_out, xor_4_out;

  not not_1 (not_1_out, x1);
  not not_2 (not_2_out, x2);
  not not_3 (not_3_out, x3);
  not not_4 (not_4_out, x4);
  xor xor_1 (xor_1_out, x1, y1);
  and and_1 (and_1_out, y1, not_1_out);
  xor xor_2 (xor_2_out, x2, y2);
  and and_2 (and_2_out, y2, not_2_out);
  xor xor_3 (xor_3_out, x3, y3);
  and and_3 (and_3_out, y3, not_3_out);
  xor xor_4 (xor_4_out, x4, y4);
  and and_4 (and_4_out, y4, not_4_out);
  not not_5 (not_5_out, xor_1_out);
  not not_6 (not_6_out, xor_2_out);
  not not_7 (not_7_out, xor_3_out);
  not not_8 (not_8_out, xor_4_out);
  xor xor_5 (D1, Bin, xor_1_out);
  and and_5 (and_5_out, not_5_out, Bin);
  xor xor_6 (D2, or_1_out, xor_2_out);
  and and_6 (and_6_out, not_6_out, or_1_out);
  xor xor_7 (D3, or_2_out, xor_3_out);
  and and_7 (and_7_out, not_7_out, or_2_out);
  xor xor_8 (D4, or_3_out, xor_4_out);
  and and_8 (and_8_out, not_8_out, or_3_out);
  or or_1 (or_1_out, and_5_out, and_1_out);
  or or_2 (or_2_out, and_6_out, and_2_out);
  or or_3 (or_3_out, and_7_out, and_3_out);
  or or_4 (Bout4, and_8_out, and_4_out);

  // Notes on the sheet:
  //   Bout1
  //   Bout2
  //   Bout3
endmodule
