// Logisim project 8-bit Full Adder.circ as structural Verilog: 1 circuit, main circuit main
module main (
  input  x8,
  input  y8,
  input  x7,
  input  y7,
  input  x6,
  input  y6,
  input  x5,
  input  y5,
  input  x4,
  input  y4,
  input  x3,
  input  y3,
  input  x2,
  input  y2,
  input  x1,
  input  y1,
  input  Cin,
  output S8,
  output Cout8,
  output S7,
  output S6,
  output S5,
  output S4,
  output S3,
  output S2,
  output S1
);

  wire and_1_out, and_2_out, and_3_out, and_4_out, and_5_out, and_6_out, and_7_out, and_8_out, and_9_out,
       and_10_out, and_11_out, and_12_out, and_13_out, and_14_out, and_15_out, and_16_out, or_2_out,
       or_3_out, or_4_out, or_5_out, or_6_out, or_7_out, or_8_out, xor_1_out, xor_2_out, xor_3_out,
       xor_4_out, xor_5_out, xor_6_out, xor_7_out, xor_8_out;

  and and_1 (and_1_out, x7, y7);
  xor xor_1 (xor_1_out, x8, y8);
  and and_2 (and_2_out, x8, y8);
  xor xor_2 (xor_2_out, x7, y7);
  xor xor_3 (xor_3_out, x6, y6);
  and and_3 (and_3_out, x6, y6);
  xor xor_4 (xor_4_out, x5, y5);
  and and_4 (and_4_out, x5, y5);
  xor xor_5 (xor_5_out, x4, y4);
  and and_5 (and_5_out, x4, y4);
  xor xor_6 (xor_6_out, x3, y3);
  and and_6 (and_6_out, x3, y3);
  xor xor_7 (xor_7_out, x2, y2);
  and and_7 (and_7_out, x2, y2);
  xor xor_8 (xor_8_out, x1, y1);
  and and_8 (and_8_out, x1, y1);
  xor xor_9 (S8, xor_1_out, or_2_out);
  and and_9 (and_9_out, xor_1_out, or_2_out);
  xor xor_10 (S7, xor_2_out, or_3_out);
  and and_10 (and_10_out, xor_2_out, or_3_out);
  xor xor_11 (S6, xor_3_out, or_4_out);
  and and_11 (and_11_out, xor_3_out, or_4_out);
  xor xor_12 (S5, xor_4_out, or_5_out);
  and and_12 (and_12_out, xor_4_out, or_5_out);
  xor xor_13 (S4, xor_5_out, or_6_out);
  and and_13 (and_13_out, xor_5_out, or_6_out);
  xor xor_14 (S3, xor_6_out, or_7_out);
  and and_14 (and_14_out, xor_6_out, or_7_out);
  xor xor_15 (S2, xor_7_out, or_8_out);
  and and_15 (and_15_out, xor_7_out, or_8_out);
  xor xor_16 (S1, xor_8_out, Cin);
  and and_16 (and_16_out, xor_8_out, Cin);
  or or_1 (Cout8, and_9_out, and_2_out);
  or or_2 (or_2_out, and_10_out, and_1_out);
  or or_3 (or_3_out, and_11_out, and_3_out);
  or or_4 (or_4_out, and_12_out, and_4_out);
  or or_5 (or_5_out, and_13_out, and_5_out);
  or or_6 (or_6_out, and_14_out, and_6_out);
  or or_7 (or_7_out, and_15_out, and_7_out);
  or or_8 (or_8_out, and_16_out, and_8_out);

  // Notes on the sheet:
  //   Cout7
  //   Cout6
  //   Cout5
  //   Cout4
  //   Cout3
  //   Cout2
  //   Cout1
endmodule
