// Logisim project SUB.circ as structural Verilog: 3 circuits, main circuit main
module main (
  input  [7:0] in_1,
  input  [15:0] in_2,
  input  in_3,
  input  in_4,
  input  in_5,
  input  in_6,
  input  in_7,
  input  in_8,
  input  [7:0] in_9,
  input  [15:0] in_10,
  input  in_11,
  input  in_12,
  input  in_13,
  input  in_14,
  input  in_15,
  input  in_16,
  input  Add_0__Sub_1,
  input  [7:0] in_18,
  input  [15:0] in_19,
  input  in_20,
  input  in_21,
  input  in_22,
  input  in_23,
  input  in_24,
  input  in_25,
  input  in_26,
  input  in_27,
  input  in_28,
  input  in_29,
  input  in_30,
  input  in_31,
  input  in_32,
  input  in_33,
  input  in_34,
  input  in_35,
  input  in_36,
  input  in_37,
  input  in_38,
  input  in_39,
  input  in_40,
  input  in_41,
  input  Add_0__Sub_1_2,
  output [15:0] out_43,
  output [15:0] out_44,
  output Co,
  output out_46,
  output out_47,
  output out_48,
  output out_49,
  output out_50,
  output out_51,
  output out_52,
  output out_53,
  output out_54,
  output out_55,
  output out_56,
  output out_57,
  output out_58,
  output out_59,
  output out_60,
  output out_61,
  output [15:0] out_62,
  output Co_2,
  output out_64,
  output out_65,
  output out_66,
  output out_67,
  output out_68,
  output out_69,
  output out_70,
  output out_71,
  output out_72,
  output out_73,
  output out_74,
  output out_75,
  output out_76,
  output out_77,
  output out_78,
  output out_79
);

  wire clock_1_out, clock_2_out, clock_3_out, clock_4_out, clock_5_out, clock_6_out, full_adder_2_co,
       full_adder_4_co, full_adder_5_co, full_adder_6_co, full_adder_7_co, full_adder_8_co, full_adder_9_co,
       full_adder_10_co, full_adder_11_co, full_adder_12_co, full_adder_13_co, full_adder_14_co,
       full_adder_15_co, full_adder_16_co, full_adder_17_co, full_adder_18_co, full_adder_19_co,
       full_adder_20_co, full_adder_21_co, full_adder_22_co, full_adder_23_co, full_adder_24_co,
       full_adder_25_co, full_adder_26_co, full_adder_27_co, full_adder_28_co, full_adder_29_co,
       full_adder_30_co, full_adder_31_co, full_adder_32_co, xor_1_out, xor_2_out, xor_3_out, xor_4_out,
       xor_5_out, xor_6_out, xor_7_out, xor_8_out, xor_9_out, xor_10_out, xor_11_out, xor_12_out, xor_13_out,
       xor_14_out, xor_15_out, xor_16_out, xor_17_out, xor_18_out, xor_19_out, xor_20_out, xor_21_out,
       xor_22_out, xor_23_out, xor_24_out, xor_25_out, xor_26_out, xor_27_out, xor_28_out, xor_29_out,
       xor_30_out, xor_31_out, xor_32_out;
  wire [15:0] ram_1_data, ram_2_data, ram_3_data;

  xor xor_1 (xor_1_out, out_44[15], Add_0__Sub_1);
  Full_Adder full_adder_1 (.A(xor_1_out), .B(out_43[15]), .Ci(full_adder_2_co), .Co(Co), .S(out_46));
  Clock clock_1 (.out(clock_1_out));
  xor xor_2 (xor_2_out, out_44[14], Add_0__Sub_1);
  Full_Adder full_adder_2 (.A(xor_2_out), .B(out_43[14]), .Ci(full_adder_4_co), .Co(full_adder_2_co), .S(out_47));
  xor xor_3 (xor_3_out, in_26, Add_0__Sub_1_2);
  Full_Adder full_adder_3 (.A(xor_3_out), .B(out_62[15]), .Ci(full_adder_5_co), .Co(Co_2), .S(out_64));
  RAM #(.dataWidth(16), .bus("separate")) ram_1 (
    .addr(in_1), .din(in_2), .data(ram_1_data), .str(in_4), .sel(in_5), .clk(clock_1_out), .ld(in_6),
    .clr(in_7));
  Clock clock_2 (.out(clock_2_out));
  xor xor_4 (xor_4_out, out_44[13], Add_0__Sub_1);
  Full_Adder full_adder_4 (.A(xor_4_out), .B(out_43[13]), .Ci(full_adder_6_co), .Co(full_adder_4_co), .S(out_48));
  Clock clock_3 (.out(clock_3_out));
  xor xor_5 (xor_5_out, in_27, Add_0__Sub_1_2);
  Full_Adder full_adder_5 (.A(xor_5_out), .B(out_62[14]), .Ci(full_adder_7_co), .Co(full_adder_5_co), .S(out_65));
  Register #(.width(16)) register_1 (.D(ram_1_data), .en(in_3), .Q(out_43), .clk(clock_2_out), .clr(in_8));
  xor xor_6 (xor_6_out, out_44[12], Add_0__Sub_1);
  Full_Adder full_adder_6 (.A(xor_6_out), .B(out_43[12]), .Ci(full_adder_8_co), .Co(full_adder_6_co), .S(out_49));
  RAM #(.dataWidth(16), .bus("separate")) ram_2 (
    .addr(in_18), .din(in_19), .data(ram_2_data), .str(in_21), .sel(in_22), .clk(clock_3_out), .ld(in_23),
    .clr(in_24));
  xor xor_7 (xor_7_out, in_28, Add_0__Sub_1_2);
  Full_Adder full_adder_7 (.A(xor_7_out), .B(out_62[13]), .Ci(full_adder_9_co), .Co(full_adder_7_co), .S(out_66));
  Register #(.width(16)) register_2 (.D(ram_2_data), .en(in_20), .Q(out_62), .clk(clock_4_out), .clr(in_25));
  Clock clock_4 (.out(clock_4_out));
  xor xor_8 (xor_8_out, out_44[11], Add_0__Sub_1);
  Full_Adder full_adder_8 (.A(xor_8_out), .B(out_43[11]), .Ci(full_adder_10_co), .Co(full_adder_8_co), .S(out_50));
  xor xor_9 (xor_9_out, in_29, Add_0__Sub_1_2);
  Full_Adder full_adder_9 (.A(xor_9_out), .B(out_62[12]), .Ci(full_adder_11_co), .Co(full_adder_9_co), .S(out_67));
  xor xor_10 (xor_10_out, out_44[10], Add_0__Sub_1);
  Full_Adder full_adder_10 (.A(xor_10_out), .B(out_43[10]), .Ci(full_adder_12_co), .Co(full_adder_10_co), .S(out_51));
  xor xor_11 (xor_11_out, in_30, Add_0__Sub_1_2);
  Full_Adder full_adder_11 (.A(xor_11_out), .B(out_62[11]), .Ci(full_adder_13_co), .Co(full_adder_11_co), .S(out_68));
  xor xor_12 (xor_12_out, out_44[9], Add_0__Sub_1);
  Full_Adder full_adder_12 (.A(xor_12_out), .B(out_43[9]), .Ci(full_adder_14_co), .Co(full_adder_12_co), .S(out_52));
  xor xor_13 (xor_13_out, in_31, Add_0__Sub_1_2);
  Full_Adder full_adder_13 (.A(xor_13_out), .B(out_62[10]), .Ci(full_adder_15_co), .Co(full_adder_13_co), .S(out_69));
  xor xor_14 (xor_14_out, out_44[8], Add_0__Sub_1);
  Full_Adder full_adder_14 (.A(xor_14_out), .B(out_43[8]), .Ci(full_adder_16_co), .Co(full_adder_14_co), .S(out_53));
  xor xor_15 (xor_15_out, in_32, Add_0__Sub_1_2);
  Full_Adder full_adder_15 (.A(xor_15_out), .B(out_62[9]), .Ci(full_adder_17_co), .Co(full_adder_15_co), .S(out_70));
  Clock clock_5 (.out(clock_5_out));
  xor xor_16 (xor_16_out, out_44[7], Add_0__Sub_1);
  Full_Adder full_adder_16 (.A(xor_16_out), .B(out_43[7]), .Ci(full_adder_18_co), .Co(full_adder_16_co), .S(out_54));
  xor xor_17 (xor_17_out, in_33, Add_0__Sub_1_2);
  Full_Adder full_adder_17 (.A(xor_17_out), .B(out_62[8]), .Ci(full_adder_19_co), .Co(full_adder_17_co), .S(out_71));
  RAM #(.dataWidth(16), .bus("separate")) ram_3 (
    .addr(in_9), .din(in_10), .data(ram_3_data), .str(in_12), .sel(in_13), .clk(clock_5_out), .ld(in_14),
    .clr(in_15));
  xor xor_18 (xor_18_out, out_44[6], Add_0__Sub_1);
  Full_Adder full_adder_18 (.A(xor_18_out), .B(out_43[6]), .Ci(full_adder_20_co), .Co(full_adder_18_co), .S(out_55));
  xor xor_19 (xor_19_out, in_34, Add_0__Sub_1_2);
  Full_Adder full_adder_19 (.A(xor_19_out), .B(out_62[7]), .Ci(full_adder_21_co), .Co(full_adder_19_co), .S(out_72));
  Register #(.width(16)) register_3 (.D(ram_3_data), .en(in_11), .Q(out_44), .clk(clock_6_out), .clr(in_16));
  Clock clock_6 (.out(clock_6_out));
  xor xor_20 (xor_20_out, out_44[5], Add_0__Sub_1);
  Full_Adder full_adder_20 (.A(xor_20_out), .B(out_43[5]), .Ci(full_adder_22_co), .Co(full_adder_20_co), .S(out_56));
  xor xor_21 (xor_21_out, in_35, Add_0__Sub_1_2);
  Full_Adder full_adder_21 (.A(xor_21_out), .B(out_62[6]), .Ci(full_adder_23_co), .Co(full_adder_21_co), .S(out_73));
  xor xor_22 (xor_22_out, out_44[4], Add_0__Sub_1);
  Full_Adder full_adder_22 (.A(xor_22_out), .B(out_43[4]), .Ci(full_adder_24_co), .Co(full_adder_22_co), .S(out_57));
  xor xor_23 (xor_23_out, in_36, Add_0__Sub_1_2);
  Full_Adder full_adder_23 (.A(xor_23_out), .B(out_62[5]), .Ci(full_adder_25_co), .Co(full_adder_23_co), .S(out_74));
  xor xor_24 (xor_24_out, out_44[3], Add_0__Sub_1);
  Full_Adder full_adder_24 (.A(xor_24_out), .B(out_43[3]), .Ci(full_adder_26_co), .Co(full_adder_24_co), .S(out_58));
  xor xor_25 (xor_25_out, in_37, Add_0__Sub_1_2);
  Full_Adder full_adder_25 (.A(xor_25_out), .B(out_62[4]), .Ci(full_adder_27_co), .Co(full_adder_25_co), .S(out_75));
  xor xor_26 (xor_26_out, out_44[2], Add_0__Sub_1);
  Full_Adder full_adder_26 (.A(xor_26_out), .B(out_43[2]), .Ci(full_adder_28_co), .Co(full_adder_26_co), .S(out_59));
  xor xor_27 (xor_27_out, in_38, Add_0__Sub_1_2);
  Full_Adder full_adder_27 (.A(xor_27_out), .B(out_62[3]), .Ci(full_adder_29_co), .Co(full_adder_27_co), .S(out_76));
  xor xor_28 (xor_28_out, out_44[1], Add_0__Sub_1);
  Full_Adder full_adder_28 (.A(xor_28_out), .B(out_43[1]), .Ci(full_adder_30_co), .Co(full_adder_28_co), .S(out_60));
  xor xor_29 (xor_29_out, in_39, Add_0__Sub_1_2);
  Full_Adder full_adder_29 (.A(xor_29_out), .B(out_62[2]), .Ci(full_adder_31_co), .Co(full_adder_29_co), .S(out_77));
  xor xor_30 (xor_30_out, out_44[0], Add_0__Sub_1);
  Full_Adder full_adder_30 (.A(xor_30_out), .B(out_43[0]), .Ci(Add_0__Sub_1), .Co(full_adder_30_co), .S(out_61));
  xor xor_31 (xor_31_out, in_40, Add_0__Sub_1_2);
  Full_Adder full_adder_31 (.A(xor_31_out), .B(out_62[1]), .Ci(full_adder_32_co), .Co(full_adder_31_co), .S(out_78));
  xor xor_32 (xor_32_out, in_41, Add_0__Sub_1_2);
  Full_Adder full_adder_32 (.A(xor_32_out), .B(out_62[0]), .Ci(Add_0__Sub_1_2), .Co(full_adder_32_co), .S(out_79));
  // AND_Gate and_1 is placed but not wired
  // AND_Gate and_2 is placed but not wired

  // Notes on the sheet:
  //   Co
  //   Ci
  //   Co
  //   Co
  //   RAM - A
  //   Ci
  //   Ci
  //   Ci
  //   Co
  //   RAM - A
  //   Ci
  //   Co
  //   Co
  //   Co
  //   Ci
  //   Co
  //   Ci
  //   Co
  //   Ci
  //   Co
  //   Ci
  //   Co
  //   Ci
  //   Ci
  //   Ci
  //   Co
  //   Ci
  //   Co
  //   Co
  //   Co
  //   Co
  //   Ci
  //   Co
  //   Ci
  //   Co
  //   Co
  //   RAM - B
  //   Ci
  //   Co
  //   Ci
  //   Co
  //   Ci
  //   Ci
  //   Ci
  //   Co
  //   Ci
  //   Co
  //   Co
  //   Co
  //   Ci
  //   Co
  //   Ci
  //   Co
  //   Ci
  //   Co
  //   Ci
  //   Co
  //   Ci
  //   Ci
  //   Ci
  //   Co
  //   Ci
  //   Co
  //   Co
  //   Co
  //   Ci
  //   Ci
  //   Co
  //   Ci
endmodule

module Full_Adder (
  input  Ci,
  input  A,
  input  B,
  output S,
  output Co
);

  wire and_1_out, and_2_out, xor_1_out;

  xor xor_1 (xor_1_out, A, B);
  and and_1 (and_1_out, xor_1_out, Ci);
  and and_2 (and_2_out, A, B);
  xor xor_2 (S, xor_1_out, Ci);
  or or_1 (Co, and_1_out, and_2_out);
endmodule

module Operation (
  input  a,
  input  b,
  output Add,
  output Sub,
  output OR,
  output NOT
);

  wire not_1_out, not_2_out, not_3_out, not_4_out;

  not not_1 (not_1_out, a);
  not not_2 (not_2_out, b);
  not not_3 (not_3_out, a);
  not not_4 (not_4_out, b);
  and and_1 (NOT, a, b);
  and and_2 (Add, not_1_out, not_2_out);
  and and_3 (Sub, not_3_out, b);
  and and_4 (OR, a, not_4_out);
endmodule
