// Logisim project NOT.circ as structural Verilog: 1 circuit, main circuit main
module main (
  input  [7:0] in_1,
  input  [15:0] in_2,
  input  in_3,
  input  in_4,
  input  in_5,
  input  in_6,
  input  in_7,
  input  in_8,
  output [15:0] out_9,
  output out_10,
  output out_11,
  output out_12,
  output out_13,
  output out_14,
  output out_15,
  output out_16,
  output out_17,
  output out_18,
  output out_19,
  output out_20,
  output out_21,
  output out_22,
  output out_23,
  output out_24,
  output out_25
);

  wire clock_1_out, clock_2_out;
  wire [15:0] ram_1_data;

  Clock clock_1 (.out(clock_1_out));
  RAM #(.dataWidth(16), .bus("separate")) ram_1 (
    .addr(in_1), .din(in_2), .data(ram_1_data), .str(in_4), .sel(in_5), .clk(clock_1_out), .ld(in_6),
    .clr(in_7));
  Clock clock_2 (.out(clock_2_out));
  not not_1 (out_10, out_9[15]);
  Register #(.width(16)) register_1 (.D(ram_1_data), .en(in_3), .Q(out_9), .clk(clock_2_out), .clr(in_8));
  not not_2 (out_14, out_9[11]);
  not not_3 (out_11, out_9[14]);
  not not_4 (out_13, out_9[12]);
  not not_5 (out_12, out_9[13]);
  not not_6 (out_16, out_9[9]);
  not not_7 (out_17, out_9[8]);
  not not_8 (out_18, out_9[7]);
  not not_9 (out_15, out_9[10]);
  not not_10 (out_19, out_9[6]);
  not not_11 (out_21, out_9[4]);
  not not_12 (out_22, out_9[3]);
  not not_13 (out_20, out_9[5]);
  not not_14 (out_23, out_9[2]);
  not not_15 (out_25, out_9[0]);
  not not_16 (out_24, out_9[1]);
  // AND_Gate and_1 is placed but not wired

  // Notes on the sheet:
  //   RAM - A
endmodule
