// Logisim project OR.circ as structural Verilog: 1 circuit, main circuit main
module main (
  input  [7:0] in_1,
  input  [15:0] in_2,
  input  in_3,
  input  in_4,
  input  in_5,
  input  in_6,
  input  in_7,
  input  in_8,
  input  [7:0] in_9,
  input  [15:0] in_10,
  input  in_11,
  input  in_12,
  input  in_13,
  input  in_14,
  input  in_15,
  input  in_16,
  output [15:0] out_17,
  output [15:0] out_18,
  output out_19,
  output out_20,
  output out_21,
  output out_22,
  output out_23,
  output out_24,
  output out_25,
  output out_26,
  output out_27,
  output out_28,
  output out_29,
  output out_30,
  output out_31,
  output out_32,
  output out_33,
  output out_34
);

  wire clock_1_out, clock_2_out, clock_3_out, clock_4_out;
  wire [15:0] ram_1_data, ram_2_data;

  or or_1 (out_19, out_17[15], out_18[15]);
  Clock clock_1 (.out(clock_1_out));
  or or_2 (out_20, out_17[14], out_18[14]);
  RAM #(.dataWidth(16), .bus("separate")) ram_1 (
    .addr(in_1), .din(in_2), .data(ram_1_data), .str(in_4), .sel(in_5), .clk(clock_1_out), .ld(in_6),
    .clr(in_7));
  Clock clock_2 (.out(clock_2_out));
  or or_3 (out_21, out_17[13], out_18[13]);
  Register #(.width(16)) register_1 (.D(ram_1_data), .en(in_3), .Q(out_17), .clk(clock_2_out), .clr(in_8));
  or or_4 (out_22, out_17[12], out_18[12]);
  or or_5 (out_23, out_17[11], out_18[11]);
  or or_6 (out_24, out_17[10], out_18[10]);
  or or_7 (out_25, out_17[9], out_18[9]);
  or or_8 (out_26, out_17[8], out_18[8]);
  or or_9 (out_27, out_17[7], out_18[7]);
  Clock clock_3 (.out(clock_3_out));
  RAM #(.dataWidth(16), .bus("separate")) ram_2 (
    .addr(in_9), .din(in_10), .data(ram_2_data), .str(in_12), .sel(in_13), .clk(clock_3_out), .ld(in_14),
    .clr(in_15));
  or or_10 (out_28, out_17[6], out_18[6]);
  Register #(.width(16)) register_2 (.D(ram_2_data), .en(in_11), .Q(out_18), .clk(clock_4_out), .clr(in_16));
  Clock clock_4 (.out(clock_4_out));
  or or_11 (out_29, out_17[5], out_18[5]);
  or or_12 (out_30, out_17[4], out_18[4]);
  or or_13 (out_31, out_17[3], out_18[3]);
  or or_14 (out_32, out_17[2], out_18[2]);
  or or_15 (out_33, out_17[1], out_18[1]);
  or or_16 (out_34, out_17[0], out_18[0]);
  // AND_Gate and_1 is placed but not wired

  // Notes on the sheet:
  //   RAM - A
  //   RAM - B
endmodule
